// Logisim project Circuito.circ as structural Verilog: 1 circuit, main circuit main
module main (
  input  A,
  input  B,
  output X
);

  wire nand_1_out, not_1_out, or_1_out;

  not not_1 (not_1_out, B);
  or or_1 (or_1_out, B, A);
  nand nand_1 (nand_1_out, not_1_out, or_1_out);
  not not_2 (X, nand_1_out);
endmodule
